# Fritzing sketch Spooler, Fan Driver (saved by Fritzing 0.9.7b)
perfboards: 1

parts:
  Q1 = Basic FET N-Channel [package="TO220 [THT]"]
  D1 = Rectifier Diode [part_number=1N4001 package="300 mil [THT]"]
  D2 = Rectifier Diode [part_number=1N4001 package="300 mil [THT]"]
  J2 = Screw terminal - 2 pins [package=THT]  # not connected
  J3 = Screw terminal - 2 pins [package=THT]  # not connected
  J5 = Screw terminal - 2 pins [package=THT]  # not connected
  R1 = Resistor [tolerance=±5% power=0.25 resistance=10k package=THT]
  J6 = Screw terminal - 2 pins [package=THT]  # not connected
  J7 = Screw terminal - 2 pins [package=THT]  # not connected
  Q2 = Basic FET N-Channel [package="TO220 [THT]"]
  R2 = Resistor [tolerance=±5% power=0.25 resistance=10k package=THT]
  D3 = Rectifier Diode [part_number=1N4001 package="300 mil [THT]"]
  D4 = Rectifier Diode [part_number=1N4001 package="300 mil [THT]"]
  J9 = Screw terminal - 2 pins [package=THT]  # not connected
  R3 = Resistor [tolerance=±5% power=0.25 resistance=150 package=THT]

nets:
  N1: Q1.gate, R1.Pin_1, R3.Pin_0
  N2: Q1.drain, D2.cathode
  N3: Q1.source, R1.Pin_0
  N4: D1.anode, D2.anode
  N5: Q2.gate, R2.Pin_1
  N6: Q2.drain, D4.cathode
  N7: Q2.source, R2.Pin_0
  N8: D3.anode, D4.anode

notes:
  Left Terminals:
  Top: 5V, Gnd
  Mid: 5V Motor
  Low: Signal, Gnd
  Right Terminals:
  Top: 12V, Gnd
  Mid: 12V Motor
  Low: Signal, Gnd
